# Fritzing sketch arduino_nodetank (saved by Fritzing 0.9.3b)

parts:
  Part1 = Arduino Uno (Rev3)  # not connected
  M1 = DC Motor
  M2 = DC Motor
  M3 = DC Motor
  M4 = DC Motor
  Part3 = Bluetooth HC-05 Macho
  J1 = Basic Servo
  Part4 = Adafruit Motor/Stepper/Servo Shield [part_number="Adafruit #1438"]
  J2 = Basic Servo
  J3 = Basic Servo

nets:
  N1: M1.pin_1, Part4.M3A
  N2: M1.pin_2, Part4.M3B
  N3: M2.pin_1, Part4.M4A
  N4: M2.pin_2, Part4.M4B
  N5: M3.pin_1, Part4.M1B
  N6: M3.pin_2, Part4.M1A
  N7: M4.pin_1, Part4.M2B
  N8: M4.pin_2, Part4.M2A
  N9: Part3.TXD, Part4.D0
  VCC: Part3.VCC, J1.vcc, Part4.+5V, J2.vcc
  GND: Part3.GND, J1.gnd, Part4.GND, J2.pulse, J3.gnd
  N10: J1.pulse, Part4.D10
  N11: Part4.D9, J2.gnd
  N12: Part4.D3, J3.pulse
  N13: Part4.IOREF, J3.vcc

custom parts:
  Adafruit Motor/Stepper/Servo Shield: The original Adafruit Motorshield kit is one of our most beloved kits, which is why we decided to make something even better. We have upgraded the shield kit to make the bestest, easiest way to drive DC and Stepper motors. This shield will make quick work of your next robotics project! We kept the ability to drive up to 4 DC motors or 2 stepper motors, but added many improvements: Instead of a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
